# Fritzing sketch PartLayout (saved by Fritzing 0.8.7b)
breadboards: 1

parts:
  Part1 = Arduino Yun
  BLINKM = Header 4 [package=molex-1x4_lock]
  LED1 = LED - 5mm [color="Red (633nm)" package="5 mm [THT]"]
  S2 = Round Pushbutton
  R1 = Resistor [tolerance=±5% resistance=220 package=THT]

nets:
  N1: Part1.D9_PWM, R1.Pin_1
  N2: Part1.D11_PWM/MOSI, S2.leg1
  N3: Part1.GND, BLINKM.1, LED1.cathode, S2.leg0
  N4: Part1.D2, BLINKM.3
  N5: Part1.D3_PWM, BLINKM.4
  N6: Part1.5V, BLINKM.2
  N7: LED1.anode, R1.Pin_0

custom parts:
  Arduino Yun: The new Arduino Yun is a microcontroller board based on the ATmega32u4 (datasheet) and the Atheros AR9331. The Atheros processor supports a Linux distribution based on OpenWRT named Linino. The board has built-in Ethernet and WiFi support, a USB-A port, micro-SD card slot, 20 digital input/output pins (of which 7 can be used as PWM outputs and 12 as analog inputs), a 16 MHz crystal oscillator,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
